// Logisim project AORPrimeri.circ as structural Verilog: 5 circuits, main circuit Moduli
module Moduli (
  input  [3:0] in_1,
  input  [3:0] in_2,
  input  [3:0] in_3,
  input  [3:0] in_4,
  input  [3:0] in_5,
  input  [1:0] in_6,
  input  [1:0] in_7,
  input  [1:0] in_8,
  input  [1:0] in_9,
  input  in_10,
  input  [1:0] in_11,
  input  [1:0] in_12,
  input  in_13,
  input  [1:0] in_14,
  input  [1:0] in_15,
  input  in_16,
  input  [1:0] in_17,
  input  [1:0] in_18,
  input  [1:0] in_19,
  input  [3:0] in_20,
  input  in_21,
  input  [31:0] in_22,
  input  in_23,
  input  in_24,
  input  in_25,
  input  [3:0] PERICA,
  input  [3:0] MASINA,
  input  [1:0] IZBORULOGA,
  input  ODIGRAJ,
  output out_30,
  output [3:0] out_31,
  output out_32,
  output [3:0] out_33,
  output out_34,
  output out_35,
  output [1:0] out_36,
  output [1:0] out_37,
  output [31:0] out_38,
  output [7:0] PARE
);

  wire clock_1_out, clock_2_out, comparator_2_eq, decoder_1_out0, decoder_1_out1, decoder_1_out2,
       decoder_1_out3, decoder_1_out4, decoder_1_out5, decoder_1_out6, decoder_1_out7, decoder_1_out8,
       decoder_1_out9, decoder_1_out10, decoder_1_out11, decoder_1_out12, decoder_1_out13, decoder_1_out14,
       decoder_1_out15, NIJEPOGODIO;
  wire [1:0] multiplexer_4_out, multiplexer_5_out;
  wire [7:0] adder_2_out, multiplexer_7_out, subtractor_1_out, ULOG;
  wire [31:8] reg32_2_dout, undriven;

  Multiplexer multiplexer_1 (.in0(in_10), .in1(in_13), .out(out_35), .sel(in_16));
  Adder #(.width(4)) adder_1 (.a(in_1), .b(in_4), .out(out_31));  // open: cin, cout
  Multiplexer #(.select(2), .width(2)) multiplexer_2 (
    .in0(in_9), .in1(in_11), .in2(in_12), .in3(in_14), .out(out_36), .sel(in_17));
  Clock clock_1 (.out(clock_1_out));
  Comparator #(.width(4)) comparator_1 (.a(in_2), .b(in_5), .gt(out_30), .eq(out_32), .lt(out_34));
  REG32 reg32_1 (.LD(in_23), .INC(in_24), .DEC(in_25), .CLK(clock_1_out), .RST(in_21), .DIN(in_22), .DOUT(out_38));
  Multiplexer #(.select(2), .width(8)) multiplexer_3 (
    .in0(8'ha), .in1(8'h14), .in2(8'h32), .in3(8'h64), .out(ULOG), .sel(IZBORULOGA));
  not not_1 (NIJEPOGODIO, comparator_2_eq);
  Comparator #(.width(4)) comparator_2 (.a(PERICA), .b(MASINA), .eq(comparator_2_eq));  // open: gt, lt
  Multiplexer #(.width(2)) multiplexer_4 (.in0(in_7), .in1(in_8), .out(multiplexer_4_out), .sel(in_19[0]));
  Multiplexer #(.width(2)) multiplexer_5 (.in0(in_15), .in1(in_18), .out(multiplexer_5_out), .sel(in_19[0]));
  Multiplexer #(.width(2)) multiplexer_6 (
    .in0(multiplexer_4_out), .in1(multiplexer_5_out), .out(out_37), .sel(in_19[1]));
  Shifter #(.width(4)) shifter_1 (.in(in_3), .\dist (in_6), .out(out_33));
  Adder adder_2 (.a(PARE), .b(ULOG), .out(adder_2_out));  // open: cin, cout
  Multiplexer #(.width(8)) multiplexer_7 (
    .in0(adder_2_out), .in1(subtractor_1_out), .out(multiplexer_7_out), .sel(NIJEPOGODIO));
  Subtractor subtractor_1 (.a(PARE), .b(ULOG), .out(subtractor_1_out));  // open: bin, bout
  Clock clock_2 (.out(clock_2_out));
  Decoder #(.enable("false"), .select(4)) decoder_1 (
    .out0(decoder_1_out0), .out1(decoder_1_out1), .out2(decoder_1_out2), .out3(decoder_1_out3),
    .out4(decoder_1_out4), .out5(decoder_1_out5), .out6(decoder_1_out6), .out7(decoder_1_out7),
    .out8(decoder_1_out8), .out9(decoder_1_out9), .out10(decoder_1_out10), .out11(decoder_1_out11),
    .out12(decoder_1_out12), .out13(decoder_1_out13), .out14(decoder_1_out14), .out15(decoder_1_out15),
    .sel(in_20));
  REG32 reg32_2 (
    .LD(ODIGRAJ), .CLK(clock_2_out), .DIN({undriven, multiplexer_7_out}), .DOUT({reg32_2_dout, PARE}));  // open: INC, DEC, RST

  // Notes on the sheet:
  //   Registar
  //   Sabirač, komparator, pomerač
  //   Multiplekser i dekoder
  //   Zadatak sa Pericom u kladionici
endmodule

module CU_TFF (
);

  wire and_1_out, and_2_out, Cgt9, CLK, incA, K1, K2, KRAJ, or_1_out, or_2_out, undriven, undriven_2,
       undriven_4, undriven_5, undriven_6, undriven_7, undriven_8, undriven_9;
  wire [1:0] t_ff_1_q;
  wire [31:0] A, adder_1_out, adder_2_out, B, C_dout, undriven_3;

  // NoConnect on undriven_2
  // NoConnect on undriven
  // NoConnect on undriven_3
  REG32 u_A (.LD(undriven), .INC(incA), .DEC(undriven_4), .CLK(CLK), .RST(undriven_2), .DIN(undriven_3), .DOUT(A));
  // NoConnect on undriven_4
  and and_1 (and_1_out, Cgt9, K2);
  and and_2 (and_2_out, ~Cgt9, K2);  // AND_Gate
  T_Flip_Flop t_ff_1 (.T(or_1_out), .clk(CLK), .Q(t_ff_1_q[0]));  // open: Qn, reset, preset
  or or_1 (or_1_out, incA, K1, and_1_out);
  T_Flip_Flop t_ff_2 (.T(or_2_out), .clk(CLK), .Q(t_ff_1_q[1]));  // open: Qn, reset, preset
  or or_2 (or_2_out, K1, and_2_out);
  // NoConnect on undriven_5
  REG32 u_B (.LD(incA), .INC(undriven_6), .DEC(undriven_7), .CLK(CLK), .RST(undriven_5), .DIN(adder_1_out), .DOUT(B));
  Decoder #(.enable("false"), .select(2)) decoder_1 (.out0(incA), .out1(K1), .out2(K2), .out3(KRAJ), .sel(t_ff_1_q));
  // NoConnect on undriven_6
  // NoConnect on undriven_7
  Adder #(.width(32)) adder_1 (.a(B), .b(32'h2), .out(adder_1_out));  // open: cin, cout
  Adder #(.width(32)) adder_2 (.a(A), .b(B), .out(adder_2_out));  // open: cin, cout
  REG32 C (.LD(K1), .INC(undriven_8), .DEC(undriven_9), .CLK(CLK), .DIN(adder_2_out), .DOUT(C_dout));  // open: RST
  // NoConnect on undriven_8
  // NoConnect on undriven_9
  Comparator #(.width(32)) comparator_1 (.a(C_dout), .b(32'h9), .gt(Cgt9));  // open: eq, lt
  Clock clock_1 (.out(CLK));

  // Other names for the same wires on the sheet: K0 = incA; ldB = incA; ldC = K1

  // Notes on the sheet:
  //   Operaciona jedinica
  //   Upravljačka jedinica
endmodule

module CU_SETAJUCA (
);

  wire and_1_out, and_2_out, Cgt9, CLK, incA, K1, K2, KRAJ, por_1_out, undriven, undriven_2, undriven_4,
       undriven_5, undriven_6, undriven_7, undriven_8, undriven_9;
  wire [31:0] A, adder_1_out, adder_2_out, B, C_dout, undriven_3;

  // NoConnect on undriven_2
  // NoConnect on undriven
  D_Flip_Flop d_ff_1 (.D(and_2_out), .clk(CLK), .Q(incA), .preset(por_1_out));  // open: Qn, reset
  // NoConnect on undriven_3
  REG32 u_A (.LD(undriven), .INC(incA), .DEC(undriven_4), .CLK(CLK), .RST(undriven_2), .DIN(undriven_3), .DOUT(A));
  // NoConnect on undriven_4
  POR por_1 (.out(por_1_out));
  D_Flip_Flop d_ff_2 (.D(incA), .clk(CLK), .Q(K1));  // open: Qn, preset, reset
  // NoConnect on undriven_5
  REG32 u_B (.LD(incA), .INC(undriven_6), .DEC(undriven_7), .CLK(CLK), .RST(undriven_5), .DIN(adder_1_out), .DOUT(B));
  D_Flip_Flop d_ff_3 (.D(K1), .clk(CLK), .Q(K2));  // open: Qn, preset, reset
  // NoConnect on undriven_6
  // NoConnect on undriven_7
  Adder #(.width(32)) adder_1 (.a(B), .b(32'h2), .out(adder_1_out));  // open: cin, cout
  and and_1 (and_1_out, K2, Cgt9);
  and and_2 (and_2_out, K2, ~Cgt9);  // AND_Gate
  D_Flip_Flop d_ff_4 (.D(and_1_out), .clk(CLK), .Q(KRAJ));  // open: Qn, preset, reset
  Adder #(.width(32)) adder_2 (.a(A), .b(B), .out(adder_2_out));  // open: cin, cout
  REG32 C (.LD(K1), .INC(undriven_8), .DEC(undriven_9), .CLK(CLK), .DIN(adder_2_out), .DOUT(C_dout));  // open: RST
  // NoConnect on undriven_8
  // NoConnect on undriven_9
  Comparator #(.width(32)) comparator_1 (.a(C_dout), .b(32'h9), .gt(Cgt9));  // open: eq, lt
  Clock clock_1 (.out(CLK));

  // Other names for the same wires on the sheet: K0 = incA; ldB = incA; ldC = K1

  // Notes on the sheet:
  //   Operaciona jedinica
  //   Upravljačka jedinica
endmodule

module CU_MC (
);

  wire and_1_out, Cgt9, CLK, decoder_1_out1, decoder_1_out2, incA, jump, ldB, ldC, not_1_out, not_2_out,
       undriven, undriven_2, undriven_3, undriven_5, undriven_6, undriven_7, undriven_8, undriven_9,
       undriven_10, undriven_11;
  wire [1:0] rom_1_data_2;
  wire [4:3] rom_1_data;
  wire [31:0] A, adder_1_out, adder_2_out, B, C_dout, reg32_1_dout, undriven_4;

  // NoConnect on undriven_2
  // NoConnect on undriven
  // NoConnect on undriven_3
  // NoConnect on undriven_4
  REG32 u_A (.LD(undriven), .INC(incA), .DEC(undriven_5), .CLK(CLK), .RST(undriven_2), .DIN(undriven_4), .DOUT(A));
  // NoConnect on undriven_5
  REG32 reg32_1 (
    .LD(jump), .INC(not_1_out), .DEC(undriven_6), .CLK(CLK), .RST(undriven_3),
    .DIN({{30{1'b0}}, rom_1_data_2}), .DOUT(reg32_1_dout));
  ROM #(.addrWidth(2), .dataWidth(7)) rom_1 (
    .addr(reg32_1_dout[1:0]), .data({rom_1_data_2, rom_1_data, ldC, ldB, incA}));
  not not_1 (not_1_out, jump);
  // NoConnect on undriven_6
  // NoConnect on undriven_7
  REG32 u_B (.LD(ldB), .INC(undriven_8), .DEC(undriven_9), .CLK(CLK), .RST(undriven_7), .DIN(adder_1_out), .DOUT(B));
  // NoConnect on undriven_8
  // NoConnect on undriven_9
  Adder #(.width(32)) adder_1 (.a(B), .b(32'h2), .out(adder_1_out));  // open: cin, cout
  Decoder #(.enable("false"), .select(2)) decoder_1 (
    .out1(decoder_1_out1), .out2(decoder_1_out2), .sel(rom_1_data));  // open: out0, out3
  Adder #(.width(32)) adder_2 (.a(A), .b(B), .out(adder_2_out));  // open: cin, cout
  REG32 C (.LD(ldC), .INC(undriven_10), .DEC(undriven_11), .CLK(CLK), .DIN(adder_2_out), .DOUT(C_dout));  // open: RST
  // NoConnect on undriven_10
  // NoConnect on undriven_11
  Comparator #(.width(32)) comparator_1 (.a(C_dout), .b(32'h9), .gt(Cgt9));  // open: eq, lt
  and and_1 (and_1_out, decoder_1_out2, not_2_out);
  not not_2 (not_2_out, Cgt9);
  or or_1 (jump, decoder_1_out1, and_1_out);
  Clock clock_1 (.out(CLK));

  // Notes on the sheet:
  //   contents of rom_1 (hex, n*v repeats v):
  //   3 4 10 68
  //   Operaciona jedinica
  //   Upravljačka jedinica
endmodule

module REG32 (
  input  [31:0] DIN,
  input  LD,
  input  INC,
  input  DEC,
  input  CLK,
  input  RST,
  output [31:0] DOUT
);

  wire or_1_out;

  or or_1 (or_1_out, INC, DEC);
  Counter #(.max('hffffffff), .width(32)) counter_1 (
    .clr(RST), .load(LD), .up(INC), .count(or_1_out), .clk(CLK), .D(DIN), .Q(DOUT));  // open: carry
endmodule
