// Logisim project PFECOMPDONE.circ as structural Verilog
module PFEBUS (
);

  wire CLK, cpu_1_rd, cpu_1_wr, RST;
  wire [31:0] cpu_1_abus, cpu_1_doutbus, mem_1_doutbus;

  Clock u_CLK (.out(CLK));
  Button button_1 (.out(RST));
  CPU cpu_1 (
    .CLK(CLK), .RST(RST), .DINBUS(mem_1_doutbus), .WR(cpu_1_wr), .RD(cpu_1_rd), .DOUTBUS(cpu_1_doutbus),
    .ABUS(cpu_1_abus));
  MEM mem_1 (
    .CLK(CLK), .WR(cpu_1_wr), .RD(cpu_1_rd), .DINBUS(cpu_1_doutbus), .ABUS(cpu_1_abus),
    .DOUTBUS(mem_1_doutbus));
  KP1 kp1_1 (
    .CLK(CLK), .WR(cpu_1_wr), .RD(cpu_1_rd), .DINBUS(cpu_1_doutbus), .ABUS(cpu_1_abus),
    .DOUTBUS(mem_1_doutbus));
endmodule

module CPU (
  input  [31:0] DINBUS,
  input  CLK,
  input  RST,
  output [31:0] ABUS,
  output [31:0] DOUTBUS,
  output WR,
  output RD
);

  wire and_1_out, and_2_out, and_3_out, and_4_out, BRANCH_exception, d_ff_1_q, decode_1_branch,
       decode_1_done, decode_1_load, decode_1_op, decode_1_op_imm, DECODE_exception, DONE_BRANCH, DONE_LOAD,
       DONE_OP, exception, fetch_1_done, or_1_out, or_2_out, or_3_out, undriven, undriven_2, undriven_3;
  wire [3:0] aluOP, decode_1_func;
  wire [4:0] decode_1_dest, decode_1_src1, decode_1_src2, REGNUM;
  wire [11:0] decode_1_imm;
  wire [15:2] CONTROL;
  wire [31:0] aluA, aluB, aluC, fetch_1_outir, inPC, inREG, outREG, PC;

  or or_1 (or_1_out, DONE_BRANCH, DONE_LOAD, DONE_OP);
  D_Flip_Flop d_ff_1 (.D(and_1_out), .clk(CLK), .Q(d_ff_1_q), .preset(RST));  // open: Qn, reset
  and and_1 (and_1_out, or_1_out, ~exception);  // AND_Gate
  REG32 u_PC (.LD(CONTROL[2]), .INC(CONTROL[3]), .DEC(undriven), .CLK(CLK), .RST(RST), .DIN(inPC), .DOUT(PC));
  // NoConnect on undriven
  FETCH fetch_1 (
    .CLK(CLK), .RST(RST), .DIN(DINBUS), .ENABLE(d_ff_1_q), .PC(PC), .CONTROL({CONTROL, WR, RD}), .A(ABUS),
    .DONE(fetch_1_done), .outIR(fetch_1_outir));
  RegWord regword_1 (
    .LD(CONTROL[4]), .INC(undriven_2), .DEC(undriven_3), .CLK(CLK), .RST(RST), .NUM(REGNUM), .DIN(inREG),
    .DOUT(outREG));
  // NoConnect on undriven_2
  // NoConnect on undriven_3
  DECODE decode_1 (
    .IR(fetch_1_outir), .ENABLE(fetch_1_done), .DONE(decode_1_done), .exception(DECODE_exception),
    .OP(decode_1_op), .OP_IMM(decode_1_op_imm), .BRANCH(decode_1_branch), .LOAD(decode_1_load),
    .DEST(decode_1_dest), .SRC1(decode_1_src1), .SRC2(decode_1_src2), .func(decode_1_func), .imm(decode_1_imm));  // open: STORE
  or or_2 (or_2_out, decode_1_op, decode_1_op_imm);
  or or_3 (or_3_out, DECODE_exception, BRANCH_exception);
  Register #(.width(1)) u_exception (.D(1'b1), .en(or_3_out), .clk(CLK), .Q(exception), .clr(RST));
  and and_2 (and_2_out, decode_1_done, or_2_out);
  and and_3 (and_3_out, decode_1_branch, decode_1_done);
  and and_4 (and_4_out, decode_1_load, decode_1_done);
  OP op_1 (
    .CLK(CLK), .RST(RST), .IS_IMM(decode_1_op_imm), .ENABLE(and_2_out), .DEST(decode_1_dest),
    .SRC1(decode_1_src1), .SRC2(decode_1_src2), .func(decode_1_func), .imm(decode_1_imm), .outREG(outREG),
    .aluC(aluC), .DONE(DONE_OP), .CONTROL({CONTROL, WR, RD}), .REGNUM(REGNUM), .inREG(inREG), .aluA(aluA),
    .aluB(aluB), .aluOp(aluOP));
  BRANCH branch_1 (
    .CLK(CLK), .RST(RST), .ENABLE(and_3_out), .SRC1(decode_1_src1), .SRC2(decode_1_src2),
    .func(decode_1_func), .imm(decode_1_imm), .PC(PC), .outREG(outREG), .aluC(aluC), .DONE(DONE_BRANCH),
    .exception(BRANCH_exception), .CONTROL({CONTROL, WR, RD}), .REGNUM(REGNUM), .inPC(inPC), .aluA(aluA),
    .aluB(aluB), .aluOp(aluOP));
  LOAD load_1 (
    .CLK(CLK), .RST(RST), .ENABLE(and_4_out), .SRC1(decode_1_src1), .dest(decode_1_dest),
    .func(decode_1_func), .imm(decode_1_imm), .outREG(outREG), .aluC(aluC), .DIN(DINBUS), .DONE(DONE_LOAD),
    .CONTROL({CONTROL, WR, RD}), .REGNUM(REGNUM), .inREG(inREG), .aluA(aluA), .aluB(aluB), .aluOp(aluOP),
    .A(ABUS));
  ALU alu_1 (.A(aluA), .B(aluB), .OP(aluOP), .C(aluC));

  // Other names for the same wires on the sheet: A[31:0] = ABUS; CONTROL[1:0] = {WR, RD}; ldPC = CONTROL[2];
  //   incPC = CONTROL[3]; ldREG = CONTROL[4]; DIN[31:0] = DINBUS; DOUT[31:0] = DOUTBUS

  // Notes on the sheet:
  //   WR: pull=down
  //   RD: pull=down
endmodule

module MEM (
  input  [31:0] ABUS,
  input  [31:0] DINBUS,
  input  CLK,
  input  WR,
  input  RD,
  output [31:0] DOUTBUS
);

  wire comparator_1_eq, OE, WE;
  wire [31:0] ram_1_dout;

  Comparator comparator_1 (.a(ABUS[31:24]), .b({8{1'b0}}), .eq(comparator_1_eq));  // open: gt, lt
  and and_1 (WE, WR, comparator_1_eq);
  and and_2 (OE, comparator_1_eq, RD);
  RAM #(.addrWidth(16), .byteenables("byteEnables"), .dataWidth(32)) ram_1 (
    .addr(ABUS[15:0]), .we(WE), .oe(OE), .clk(CLK), .din(DINBUS), .dout(ram_1_dout), .be3(ABUS[19]),
    .be2(ABUS[18]), .be1(ABUS[17]), .be0(ABUS[16]));
  assign DOUTBUS = OE ? ram_1_dout : 32'bz;  // Controlled_Buffer controlled_buffer_1

  // Other names for the same wires on the sheet: A[31:0] = ABUS; MEMADR[15:0] = ABUS[15:0]; BE0 = ABUS[16];
  //   BE1 = ABUS[17]; BE2 = ABUS[18]; BE3 = ABUS[19]; PERADR[7:0] = ABUS[31:24]; DIN[31:0] = DINBUS;
  //   DOUT[31:0] = DOUTBUS

  // Notes on the sheet:
  //   Upravljačka jedinica
  //   Operaciona jedinica
endmodule

module KP1 (
  input  [31:0] ABUS,
  input  [31:0] DINBUS,
  input  CLK,
  input  WR,
  input  RD,
  output [31:0] DOUTBUS
);
endmodule

module REG32 (
  input  [31:0] DIN,
  input  LD,
  input  INC,
  input  DEC,
  input  CLK,
  input  RST,
  output [31:0] DOUT
);

  wire or_1_out;

  or or_1 (or_1_out, INC, DEC);
  Counter #(.max('hffffffff), .width(32)) counter_1 (
    .clr(RST), .load(LD), .up(INC), .count(or_1_out), .clk(CLK), .D(DIN), .Q(DOUT));  // open: carry
endmodule

module RegWord (
  input  [4:0] NUM,
  input  [31:0] DIN,
  input  LD,
  input  INC,
  input  DEC,
  input  CLK,
  input  RST,
  output [31:0] DOUT
);

  wire and_1_out, and_2_out, and_3_out, and_4_out, and_5_out, and_6_out, and_7_out, and_8_out, and_9_out,
       and_10_out, and_11_out, and_12_out, and_13_out, and_14_out, and_15_out, and_16_out, and_17_out,
       and_18_out, and_19_out, and_20_out, and_21_out, and_22_out, and_23_out, and_24_out, and_25_out,
       and_26_out, and_27_out, and_28_out, and_29_out, and_30_out, and_31_out, and_32_out, and_33_out,
       and_34_out, and_35_out, and_36_out, and_37_out, and_38_out, and_39_out, and_40_out, and_41_out,
       and_42_out, and_43_out, and_44_out, and_45_out, and_46_out, and_47_out, and_48_out, and_49_out,
       and_50_out, and_51_out, and_52_out, and_53_out, and_54_out, and_55_out, and_56_out, and_57_out,
       and_58_out, and_59_out, and_60_out, and_61_out, and_62_out, and_63_out, and_64_out, and_65_out,
       and_66_out, and_67_out, and_68_out, and_69_out, and_70_out, and_71_out, and_72_out, and_73_out,
       and_74_out, and_75_out, and_76_out, and_77_out, and_78_out, and_79_out, and_80_out, and_81_out,
       and_82_out, and_83_out, and_84_out, and_85_out, and_86_out, and_87_out, and_88_out, and_89_out,
       and_90_out, and_91_out, and_92_out, and_93_out, R0, R1, R2, R3, R4, R5, R6, R7, R8, R9, R10, R11, R12,
       R13, R14, R15, R16, R17, R18, R19, R20, R21, R22, R23, R24, R25, R26, R27, R28, R29, R30, R31;
  wire [31:0] R1_dout, R2_dout, R3_dout, R4_dout, R5_dout, R6_dout, R7_dout, R8_dout, R9_dout, R10_dout,
       R11_dout, R12_dout, R13_dout, R14_dout, R15_dout, R16_dout, R17_dout, R18_dout, R19_dout, R20_dout,
       R21_dout, R22_dout, R23_dout, R24_dout, R25_dout, R26_dout, R27_dout, R28_dout, R29_dout, R30_dout,
       R31_dout;

  Decoder #(.enable("false"), .select(5)) decoder_1 (
    .out0(R0), .out1(R1), .out2(R2), .out3(R3), .out4(R4), .out5(R5), .out6(R6), .out7(R7), .out8(R8),
    .out9(R9), .out10(R10), .out11(R11), .out12(R12), .out13(R13), .out14(R14), .out15(R15), .out16(R16),
    .out17(R17), .out18(R18), .out19(R19), .out20(R20), .out21(R21), .out22(R22), .out23(R23), .out24(R24),
    .out25(R25), .out26(R26), .out27(R27), .out28(R28), .out29(R29), .out30(R30), .out31(R31), .sel(NUM));
  and and_1 (and_1_out, LD, R1);
  and and_2 (and_2_out, LD, R2);
  and and_3 (and_3_out, LD, R3);
  and and_4 (and_4_out, LD, R4);
  and and_5 (and_5_out, LD, R5);
  and and_6 (and_6_out, LD, R6);
  and and_7 (and_7_out, LD, R7);
  and and_8 (and_8_out, LD, R28);
  and and_9 (and_9_out, LD, R8);
  and and_10 (and_10_out, LD, R9);
  and and_11 (and_11_out, LD, R10);
  and and_12 (and_12_out, LD, R11);
  and and_13 (and_13_out, LD, R12);
  and and_14 (and_14_out, LD, R13);
  and and_15 (and_15_out, LD, R14);
  and and_16 (and_16_out, LD, R15);
  and and_17 (and_17_out, LD, R16);
  and and_18 (and_18_out, LD, R17);
  and and_19 (and_19_out, LD, R18);
  and and_20 (and_20_out, LD, R19);
  and and_21 (and_21_out, LD, R20);
  and and_22 (and_22_out, LD, R21);
  and and_23 (and_23_out, LD, R22);
  and and_24 (and_24_out, LD, R23);
  and and_25 (and_25_out, LD, R24);
  and and_26 (and_26_out, LD, R25);
  and and_27 (and_27_out, LD, R26);
  and and_28 (and_28_out, LD, R27);
  and and_29 (and_29_out, LD, R29);
  and and_30 (and_30_out, LD, R30);
  and and_31 (and_31_out, LD, R31);
  assign DOUT = R0 ? {32{1'b0}} : 32'bz;  // Controlled_Buffer controlled_buffer_1
  REG32 u_R1 (.LD(and_1_out), .INC(and_32_out), .DEC(and_33_out), .CLK(CLK), .RST(RST), .DIN(DIN), .DOUT(R1_dout));
  assign DOUT = R1 ? R1_dout : 32'bz;  // Controlled_Buffer controlled_buffer_2
  REG32 u_R2 (.LD(and_2_out), .INC(and_34_out), .DEC(and_35_out), .CLK(CLK), .RST(RST), .DIN(DIN), .DOUT(R2_dout));
  assign DOUT = R2 ? R2_dout : 32'bz;  // Controlled_Buffer controlled_buffer_3
  REG32 u_R3 (.LD(and_3_out), .INC(and_36_out), .DEC(and_37_out), .CLK(CLK), .RST(RST), .DIN(DIN), .DOUT(R3_dout));
  assign DOUT = R3 ? R3_dout : 32'bz;  // Controlled_Buffer controlled_buffer_4
  REG32 u_R4 (.LD(and_4_out), .INC(and_38_out), .DEC(and_39_out), .CLK(CLK), .RST(RST), .DIN(DIN), .DOUT(R4_dout));
  assign DOUT = R4 ? R4_dout : 32'bz;  // Controlled_Buffer controlled_buffer_5
  REG32 u_R5 (.LD(and_5_out), .INC(and_40_out), .DEC(and_41_out), .CLK(CLK), .RST(RST), .DIN(DIN), .DOUT(R5_dout));
  assign DOUT = R5 ? R5_dout : 32'bz;  // Controlled_Buffer controlled_buffer_6
  REG32 u_R6 (.LD(and_6_out), .INC(and_42_out), .DEC(and_43_out), .CLK(CLK), .RST(RST), .DIN(DIN), .DOUT(R6_dout));
  assign DOUT = R6 ? R6_dout : 32'bz;  // Controlled_Buffer controlled_buffer_7
  REG32 u_R7 (.LD(and_7_out), .INC(and_44_out), .DEC(and_45_out), .CLK(CLK), .RST(RST), .DIN(DIN), .DOUT(R7_dout));
  assign DOUT = R7 ? R7_dout : 32'bz;  // Controlled_Buffer controlled_buffer_8
  REG32 u_R28 (.LD(and_8_out), .INC(and_46_out), .DEC(and_47_out), .CLK(CLK), .RST(RST), .DIN(DIN), .DOUT(R28_dout));
  assign DOUT = R28 ? R28_dout : 32'bz;  // Controlled_Buffer controlled_buffer_9
  REG32 u_R8 (.LD(and_9_out), .INC(and_48_out), .DEC(and_49_out), .CLK(CLK), .RST(RST), .DIN(DIN), .DOUT(R8_dout));
  assign DOUT = R8 ? R8_dout : 32'bz;  // Controlled_Buffer controlled_buffer_10
  REG32 u_R9 (.LD(and_10_out), .INC(and_50_out), .DEC(and_51_out), .CLK(CLK), .RST(RST), .DIN(DIN), .DOUT(R9_dout));
  assign DOUT = R9 ? R9_dout : 32'bz;  // Controlled_Buffer controlled_buffer_11
  REG32 u_R10 (.LD(and_11_out), .INC(and_52_out), .DEC(and_53_out), .CLK(CLK), .RST(RST), .DIN(DIN), .DOUT(R10_dout));
  assign DOUT = R10 ? R10_dout : 32'bz;  // Controlled_Buffer controlled_buffer_12
  REG32 u_R11 (.LD(and_12_out), .INC(and_54_out), .DEC(and_55_out), .CLK(CLK), .RST(RST), .DIN(DIN), .DOUT(R11_dout));
  assign DOUT = R11 ? R11_dout : 32'bz;  // Controlled_Buffer controlled_buffer_13
  REG32 u_R12 (.LD(and_13_out), .INC(and_56_out), .DEC(and_57_out), .CLK(CLK), .RST(RST), .DIN(DIN), .DOUT(R12_dout));
  assign DOUT = R12 ? R12_dout : 32'bz;  // Controlled_Buffer controlled_buffer_14
  REG32 u_R13 (.LD(and_14_out), .INC(and_58_out), .DEC(and_59_out), .CLK(CLK), .RST(RST), .DIN(DIN), .DOUT(R13_dout));
  assign DOUT = R13 ? R13_dout : 32'bz;  // Controlled_Buffer controlled_buffer_15
  REG32 u_R14 (.LD(and_15_out), .INC(and_60_out), .DEC(and_61_out), .CLK(CLK), .RST(RST), .DIN(DIN), .DOUT(R14_dout));
  assign DOUT = R14 ? R14_dout : 32'bz;  // Controlled_Buffer controlled_buffer_16
  REG32 u_R15 (.LD(and_16_out), .INC(and_62_out), .DEC(and_63_out), .CLK(CLK), .RST(RST), .DIN(DIN), .DOUT(R15_dout));
  assign DOUT = R15 ? R15_dout : 32'bz;  // Controlled_Buffer controlled_buffer_17
  REG32 u_R16 (.LD(and_17_out), .INC(and_64_out), .DEC(and_65_out), .CLK(CLK), .RST(RST), .DIN(DIN), .DOUT(R16_dout));
  assign DOUT = R16 ? R16_dout : 32'bz;  // Controlled_Buffer controlled_buffer_18
  REG32 u_R17 (.LD(and_18_out), .INC(and_66_out), .DEC(and_67_out), .CLK(CLK), .RST(RST), .DIN(DIN), .DOUT(R17_dout));
  assign DOUT = R17 ? R17_dout : 32'bz;  // Controlled_Buffer controlled_buffer_19
  REG32 u_R18 (.LD(and_19_out), .INC(and_68_out), .DEC(and_69_out), .CLK(CLK), .RST(RST), .DIN(DIN), .DOUT(R18_dout));
  assign DOUT = R18 ? R18_dout : 32'bz;  // Controlled_Buffer controlled_buffer_20
  REG32 u_R19 (.LD(and_20_out), .INC(and_70_out), .DEC(and_71_out), .CLK(CLK), .RST(RST), .DIN(DIN), .DOUT(R19_dout));
  assign DOUT = R19 ? R19_dout : 32'bz;  // Controlled_Buffer controlled_buffer_21
  REG32 u_R20 (.LD(and_21_out), .INC(and_72_out), .DEC(and_73_out), .CLK(CLK), .RST(RST), .DIN(DIN), .DOUT(R20_dout));
  assign DOUT = R20 ? R20_dout : 32'bz;  // Controlled_Buffer controlled_buffer_22
  REG32 u_R21 (.LD(and_22_out), .INC(and_74_out), .DEC(and_75_out), .CLK(CLK), .RST(RST), .DIN(DIN), .DOUT(R21_dout));
  assign DOUT = R21 ? R21_dout : 32'bz;  // Controlled_Buffer controlled_buffer_23
  REG32 u_R22 (.LD(and_23_out), .INC(and_76_out), .DEC(and_77_out), .CLK(CLK), .RST(RST), .DIN(DIN), .DOUT(R22_dout));
  assign DOUT = R22 ? R22_dout : 32'bz;  // Controlled_Buffer controlled_buffer_24
  REG32 u_R23 (.LD(and_24_out), .INC(and_78_out), .DEC(and_79_out), .CLK(CLK), .RST(RST), .DIN(DIN), .DOUT(R23_dout));
  assign DOUT = R23 ? R23_dout : 32'bz;  // Controlled_Buffer controlled_buffer_25
  REG32 u_R24 (.LD(and_25_out), .INC(and_80_out), .DEC(and_81_out), .CLK(CLK), .RST(RST), .DIN(DIN), .DOUT(R24_dout));
  assign DOUT = R24 ? R24_dout : 32'bz;  // Controlled_Buffer controlled_buffer_26
  REG32 u_R25 (.LD(and_26_out), .INC(and_82_out), .DEC(and_83_out), .CLK(CLK), .RST(RST), .DIN(DIN), .DOUT(R25_dout));
  assign DOUT = R25 ? R25_dout : 32'bz;  // Controlled_Buffer controlled_buffer_27
  REG32 u_R26 (.LD(and_27_out), .INC(and_84_out), .DEC(and_85_out), .CLK(CLK), .RST(RST), .DIN(DIN), .DOUT(R26_dout));
  assign DOUT = R26 ? R26_dout : 32'bz;  // Controlled_Buffer controlled_buffer_28
  REG32 u_R27 (.LD(and_28_out), .INC(and_86_out), .DEC(and_87_out), .CLK(CLK), .RST(RST), .DIN(DIN), .DOUT(R27_dout));
  assign DOUT = R27 ? R27_dout : 32'bz;  // Controlled_Buffer controlled_buffer_29
  REG32 u_R29 (.LD(and_29_out), .INC(and_88_out), .DEC(and_89_out), .CLK(CLK), .RST(RST), .DIN(DIN), .DOUT(R29_dout));
  assign DOUT = R29 ? R29_dout : 32'bz;  // Controlled_Buffer controlled_buffer_30
  REG32 u_R30 (.LD(and_30_out), .INC(and_90_out), .DEC(and_91_out), .CLK(CLK), .RST(RST), .DIN(DIN), .DOUT(R30_dout));
  assign DOUT = R30 ? R30_dout : 32'bz;  // Controlled_Buffer controlled_buffer_31
  REG32 u_R31 (.LD(and_31_out), .INC(and_92_out), .DEC(and_93_out), .CLK(CLK), .RST(RST), .DIN(DIN), .DOUT(R31_dout));
  assign DOUT = R31 ? R31_dout : 32'bz;  // Controlled_Buffer controlled_buffer_32
  and and_32 (and_32_out, INC, R1);
  and and_33 (and_33_out, DEC, R1);
  and and_34 (and_34_out, INC, R2);
  and and_35 (and_35_out, DEC, R2);
  and and_36 (and_36_out, INC, R3);
  and and_37 (and_37_out, DEC, R3);
  and and_38 (and_38_out, INC, R4);
  and and_39 (and_39_out, DEC, R4);
  and and_40 (and_40_out, INC, R5);
  and and_41 (and_41_out, DEC, R5);
  and and_42 (and_42_out, INC, R6);
  and and_43 (and_43_out, DEC, R6);
  and and_44 (and_44_out, INC, R7);
  and and_45 (and_45_out, DEC, R7);
  and and_46 (and_46_out, INC, R28);
  and and_47 (and_47_out, DEC, R28);
  and and_48 (and_48_out, INC, R8);
  and and_49 (and_49_out, DEC, R8);
  and and_50 (and_50_out, INC, R9);
  and and_51 (and_51_out, DEC, R9);
  and and_52 (and_52_out, INC, R10);
  and and_53 (and_53_out, DEC, R10);
  and and_54 (and_54_out, INC, R11);
  and and_55 (and_55_out, DEC, R11);
  and and_56 (and_56_out, INC, R12);
  and and_57 (and_57_out, DEC, R12);
  and and_58 (and_58_out, INC, R13);
  and and_59 (and_59_out, DEC, R13);
  and and_60 (and_60_out, INC, R14);
  and and_61 (and_61_out, DEC, R14);
  and and_62 (and_62_out, INC, R15);
  and and_63 (and_63_out, DEC, R15);
  and and_64 (and_64_out, INC, R16);
  and and_65 (and_65_out, DEC, R16);
  and and_66 (and_66_out, INC, R17);
  and and_67 (and_67_out, DEC, R17);
  and and_68 (and_68_out, INC, R18);
  and and_69 (and_69_out, DEC, R18);
  and and_70 (and_70_out, INC, R19);
  and and_71 (and_71_out, DEC, R19);
  and and_72 (and_72_out, INC, R20);
  and and_73 (and_73_out, DEC, R20);
  and and_74 (and_74_out, INC, R21);
  and and_75 (and_75_out, DEC, R21);
  and and_76 (and_76_out, INC, R22);
  and and_77 (and_77_out, DEC, R22);
  and and_78 (and_78_out, INC, R23);
  and and_79 (and_79_out, DEC, R23);
  and and_80 (and_80_out, INC, R24);
  and and_81 (and_81_out, DEC, R24);
  and and_82 (and_82_out, INC, R25);
  and and_83 (and_83_out, DEC, R25);
  and and_84 (and_84_out, INC, R26);
  and and_85 (and_85_out, DEC, R26);
  and and_86 (and_86_out, INC, R27);
  and and_87 (and_87_out, DEC, R27);
  and and_88 (and_88_out, INC, R29);
  and and_89 (and_89_out, DEC, R29);
  and and_90 (and_90_out, INC, R30);
  and and_91 (and_91_out, DEC, R30);
  and and_92 (and_92_out, INC, R31);
  and and_93 (and_93_out, DEC, R31);
endmodule

module ALU (
  input  [31:0] A,
  input  [31:0] B,
  input  [3:0] OP,
  output [31:0] C
);

  wire AeqB, AltB, AltuB;
  wire [0:0] resBGE, resBGEU, resBNE;
  wire [31:0] resADD, resAND, resOR, resSLL, resSRA, resSRL, resSUB, resXOR;

  Adder #(.width(32)) adder_1 (.a(A), .b(B), .out(resADD));  // open: cin, cout
  Subtractor #(.width(32)) subtractor_1 (.a(A), .b(B), .out(resSUB));  // open: bin, bout
  Shifter #(.width(32)) shifter_1 (.in(A), .\dist (B[4:0]), .out(resSLL));
  Shifter #(.shift("lr"), .width(32)) shifter_2 (.in(A), .\dist (B[4:0]), .out(resSRL));
  Shifter #(.shift("ar"), .width(32)) shifter_3 (.in(A), .\dist (B[4:0]), .out(resSRA));
  Comparator #(.width(32)) comparator_1 (.a(A), .b(B), .eq(AeqB), .lt(AltB));  // open: gt
  Comparator #(.mode("unsigned"), .width(32)) comparator_2 (.a(A), .b(B), .lt(AltuB));  // open: gt, eq
  assign resOR = A | B;  // OR_Gate or_1, 32 bits wide
  assign resAND = A & B;  // AND_Gate and_1, 32 bits wide
  assign resXOR = A ^ B;  // XOR_Gate xor_1, 32 bits wide
  not not_1 (resBGE[0], AltB);
  not not_2 (resBGEU[0], AltuB);
  not not_3 (resBNE[0], AeqB);
  Multiplexer #(.select(4), .width(32)) multiplexer_1 (
    .in0(resADD), .in1(resSLL), .in2({{31{1'b0}}, AltB}), .in3({{31{1'b0}}, AltuB}), .in4(resXOR),
    .in5(resSRL), .in6(resOR), .in7(resAND), .in8(resSUB), .in9({{31{1'b0}}, AeqB}),
    .in10({{31{1'b0}}, resBNE[0]}), .in11({{31{1'b0}}, resBGE[0]}), .in12({{31{1'b0}}, resBGEU[0]}),
    .in13(resSRA), .in14(A), .in15(A), .out(C), .sel(OP));

  // Other names for the same wires on the sheet: resBEQ[0] = AeqB; resSLT[0] = AltB; resSLTU[0] = AltuB
endmodule

module FETCH (
  input  CLK,
  input  RST,
  input  [31:0] DIN,
  input  ENABLE,
  input  [31:0] PC,
  output [15:0] CONTROL,
  output [31:0] A,
  output DONE,
  output [31:0] outIR
);

  wire ldIR, RD, undriven, undriven_2;

  assign CONTROL[0] = RD ? 1'b1 : 1'bz;  // Controlled_Buffer controlled_buffer_1
  assign CONTROL[3] = ENABLE ? 1'b1 : 1'bz;  // Controlled_Buffer controlled_buffer_2
  REG32 IR (.LD(ldIR), .INC(undriven), .DEC(undriven_2), .CLK(CLK), .RST(RST), .DIN(DIN), .DOUT(outIR));
  // NoConnect on undriven
  // NoConnect on undriven_2
  D_Flip_Flop d_ff_1 (.D(ENABLE), .clk(CLK), .Q(ldIR), .reset(RST));  // open: Qn, preset
  assign A = ENABLE ? {{16{1'b0}}, PC[15:0]} : 32'bz;  // Controlled_Buffer controlled_buffer_3
  or or_1 (RD, ENABLE, ldIR);
  D_Flip_Flop d_ff_2 (.D(ldIR), .clk(CLK), .Q(DONE), .reset(RST));  // open: Qn, preset

  // Other names for the same wires on the sheet: incPC = ENABLE; IR[31:0] = outIR; STEP1 = ldIR
endmodule

module DECODE (
  input  [31:0] IR,
  input  ENABLE,
  output DONE,
  output exception,
  output OP,
  output OP_IMM,
  output BRANCH,
  output LOAD,
  output STORE,
  output [4:0] DEST,
  output [4:0] SRC1,
  output [4:0] SRC2,
  output [3:0] func,
  output [11:0] imm
);

  wire and_1_out, and_3_out, nor_1_out;

  assign imm = OP_IMM ? IR[31:20] : 12'bz;  // Controlled_Buffer controlled_buffer_1
  assign imm = BRANCH ? {IR[31], IR[7], IR[30:25], IR[11:8]} : 12'bz;  // Controlled_Buffer controlled_buffer_2
  assign imm = LOAD ? IR[31:20] : 12'bz;  // Controlled_Buffer controlled_buffer_3
  assign imm = STORE ? {IR[31:25], IR[11:7]} : 12'bz;  // Controlled_Buffer controlled_buffer_4
  Comparator #(.width(7)) comparator_1 (.a(IR[6:0]), .b(7'b0110011), .eq(OP));  // open: gt, lt
  Comparator #(.width(7)) comparator_2 (.a(IR[6:0]), .b(7'b0010011), .eq(OP_IMM));  // open: gt, lt
  Comparator #(.width(7)) comparator_3 (.a(IR[6:0]), .b(7'b1100011), .eq(BRANCH));  // open: gt, lt
  Comparator #(.width(7)) comparator_4 (.a(IR[6:0]), .b(7'b0000011), .eq(LOAD));  // open: gt, lt
  Comparator #(.width(7)) comparator_5 (.a(IR[6:0]), .b(7'b0100011), .eq(STORE));  // open: gt, lt
  nor nor_1 (nor_1_out, OP, OP_IMM, BRANCH, LOAD, STORE, 1'b0, 1'b0, 1'b0, 1'b0, 1'b0);
  Multiplexer multiplexer_1 (.in0(IR[30]), .in1(1'b0), .out(func[3]), .sel(and_1_out));
  and and_1 (and_1_out, OP_IMM, ~and_3_out);  // AND_Gate
  and and_2 (exception, nor_1_out, ENABLE);
  and and_3 (and_3_out, IR[14], ~IR[13], IR[12]);  // AND_Gate

  assign DEST = IR[11:7];
  assign DONE = ENABLE;
  assign func[2:0] = IR[14:12];
  assign SRC1 = IR[19:15];
  assign SRC2 = IR[24:20];

  // Other names for the same wires on the sheet: BRANCH_OFFSET[11:0] = {IR[31], IR[7], IR[30:25], IR[11:8]};
  //   STORE_OFFSET[11:0] = {IR[31:25], IR[11:7]}; UPPER_12[11:0] = IR[31:20]; function7_5 = IR[30];
  //   function3[2:0] = IR[14:12]; opcode[6:0] = IR[6:0]
endmodule

module OP (
  input  CLK,
  input  RST,
  input  IS_IMM,
  input  ENABLE,
  input  [4:0] DEST,
  input  [4:0] SRC1,
  input  [4:0] SRC2,
  input  [3:0] func,
  input  [11:0] imm,
  input  [31:0] outREG,
  input  [31:0] aluC,
  output DONE,
  output [15:0] CONTROL,
  output [4:0] REGNUM,
  output [31:0] inREG,
  output [31:0] aluA,
  output [31:0] aluB,
  output [3:0] aluOp
);

  wire ldB, undriven, undriven_2, undriven_3, undriven_4;
  wire [31:0] A, B, bit_extender_1_out, inB;

  assign CONTROL[4] = DONE ? 1'b1 : 1'bz;  // Controlled_Buffer controlled_buffer_1
  assign REGNUM = ENABLE ? SRC1 : 5'bz;  // Controlled_Buffer controlled_buffer_2
  assign REGNUM = ldB ? SRC2 : 5'bz;  // Controlled_Buffer controlled_buffer_3
  REG32 u_A (.LD(ENABLE), .INC(undriven), .DEC(undriven_2), .CLK(CLK), .RST(RST), .DIN(outREG), .DOUT(A));
  // NoConnect on undriven
  // NoConnect on undriven_2
  assign REGNUM = DONE ? DEST : 5'bz;  // Controlled_Buffer controlled_buffer_4
  D_Flip_Flop d_ff_1 (.D(ENABLE), .clk(CLK), .Q(ldB), .reset(RST));  // open: Qn, preset
  assign aluA = DONE ? A : 32'bz;  // Controlled_Buffer controlled_buffer_5
  assign bit_extender_1_out = {{20{imm[11]}}, imm};  // Bit_Extender bit_extender_1
  D_Flip_Flop d_ff_2 (.D(ldB), .clk(CLK), .Q(DONE), .reset(RST));  // open: Qn, preset
  // NoConnect on undriven_3
  REG32 u_B (.LD(ldB), .INC(undriven_3), .DEC(undriven_4), .CLK(CLK), .RST(RST), .DIN(inB), .DOUT(B));
  // NoConnect on undriven_4
  assign aluB = DONE ? B : 32'bz;  // Controlled_Buffer controlled_buffer_6
  Multiplexer #(.width(32)) multiplexer_1 (.in0(outREG), .in1(bit_extender_1_out), .out(inB), .sel(IS_IMM));
  assign aluOp = DONE ? func : 4'bz;  // Controlled_Buffer controlled_buffer_7
  assign inREG = DONE ? aluC : 32'bz;  // Controlled_Buffer controlled_buffer_8

  // Other names for the same wires on the sheet: inA[31:0] = outREG; ldA = ENABLE; STEP1 = ldB; ldREG = DONE
endmodule

module BRANCH (
  input  CLK,
  input  RST,
  input  ENABLE,
  input  [4:0] SRC1,
  input  [4:0] SRC2,
  input  [3:0] func,
  input  [11:0] imm,
  input  [31:0] PC,
  input  [31:0] outREG,
  input  [31:0] aluC,
  output DONE,
  output exception,
  output [15:0] CONTROL,
  output [4:0] REGNUM,
  output [31:0] inPC,
  output [31:0] aluA,
  output [31:0] aluB,
  output [3:0] aluOp
);

  wire and_3_out, BRANCH_COND, exception_decode, ldB, ldCond, ldPC, or_1_out, undriven, undriven_2,
       undriven_3, undriven_4;
  wire [3:0] branchOp;
  wire [31:0] A, B, immext, INSTRUCTION_START;

  assign CONTROL[2] = ldPC ? 1'b1 : 1'bz;  // Controlled_Buffer controlled_buffer_1
  assign REGNUM = ENABLE ? SRC1 : 5'bz;  // Controlled_Buffer controlled_buffer_2
  assign REGNUM = ldB ? SRC2 : 5'bz;  // Controlled_Buffer controlled_buffer_3
  and and_1 (ldPC, DONE, BRANCH_COND);
  or or_1 (or_1_out, imm[0], exception_decode);
  D_Flip_Flop d_ff_1 (.D(ENABLE), .clk(CLK), .Q(ldB), .reset(RST));  // open: Qn, preset
  REG32 u_A (.LD(ENABLE), .INC(undriven), .DEC(undriven_2), .CLK(CLK), .RST(RST), .DIN(outREG), .DOUT(A));
  assign aluA = ldCond ? A : 32'bz;  // Controlled_Buffer controlled_buffer_4
  and and_2 (exception, or_1_out, ENABLE);
  D_Flip_Flop d_ff_2 (.D(ldB), .clk(CLK), .Q(ldCond), .reset(RST));  // open: Qn, preset
  // NoConnect on undriven
  // NoConnect on undriven_2
  assign aluB = ldCond ? B : 32'bz;  // Controlled_Buffer controlled_buffer_5
  assign aluOp = ldCond ? branchOp : 4'bz;  // Controlled_Buffer controlled_buffer_6
  D_Flip_Flop d_ff_3 (.D(ldCond), .clk(CLK), .Q(DONE), .reset(RST));  // open: Qn, preset
  // NoConnect on undriven_3
  REG32 u_B (.LD(ldB), .INC(undriven_3), .DEC(undriven_4), .CLK(CLK), .RST(RST), .DIN(outREG), .DOUT(B));
  // NoConnect on undriven_4
  assign immext = {{21{imm[11]}}, imm[11:1]};  // Bit_Extender bit_extender_1
  assign aluA = DONE ? INSTRUCTION_START : 32'bz;  // Controlled_Buffer controlled_buffer_7
  D_Flip_Flop d_ff_4 (.D(and_3_out), .clk(CLK), .Q(BRANCH_COND));  // open: Qn, preset, reset
  and and_3 (and_3_out, ldCond, aluC[0]);
  assign aluB = DONE ? immext : 32'bz;  // Controlled_Buffer controlled_buffer_8
  Multiplexer #(.select(3), .width(4)) multiplexer_1 (
    .in0(4'b1001), .in1(4'b1010), .in2(4'b0000), .in3(4'b0000), .in4(4'b0010), .in5(4'b1001), .in6(4'b0011),
    .in7(4'b1100), .out(branchOp), .sel(func[2:0]));
  Comparator #(.width(4)) comparator_1 (.a(branchOp), .b(4'b0000), .eq(exception_decode));  // open: gt, lt
  assign inPC = DONE ? aluC : 32'bz;  // Controlled_Buffer controlled_buffer_9
  assign aluOp = DONE ? 4'b0000 : 4'bz;  // Controlled_Buffer controlled_buffer_10
  Subtractor #(.width(32)) subtractor_1 (.a(PC), .b(32'h1), .out(INSTRUCTION_START));  // open: bin, bout

  // Other names for the same wires on the sheet: exception_align = imm[0]; inA[31:0] = outREG; inB[31:0] = outREG;
  //   ldA = ENABLE; STEP1 = ldB; STEP2 = ldCond
endmodule

module LOAD (
  input  CLK,
  input  RST,
  input  ENABLE,
  input  [4:0] SRC1,
  input  [4:0] dest,
  input  [3:0] func,
  input  [11:0] imm,
  input  [31:0] outREG,
  input  [31:0] aluC,
  input  [31:0] DIN,
  output DONE,
  output [15:0] CONTROL,
  output [4:0] REGNUM,
  output [31:0] inREG,
  output [31:0] aluA,
  output [31:0] aluB,
  output [3:0] aluOp,
  output [31:0] A
);

  wire RD, undriven, undriven_2;
  wire [7:0] \byte ;
  wire [15:0] halfword;
  wire [31:0] adr, immext, resLB, resLBU, resLH, resLHU, result;

  assign CONTROL[0] = RD ? 1'b1 : 1'bz;  // Controlled_Buffer controlled_buffer_1
  assign CONTROL[4] = DONE ? 1'b1 : 1'bz;  // Controlled_Buffer controlled_buffer_2
  Multiplexer #(.width(16)) multiplexer_1 (.in0(DIN[15:0]), .in1(DIN[31:16]), .out(halfword), .sel(adr[0]));
  REG32 u_adr (.LD(ENABLE), .INC(undriven), .DEC(undriven_2), .CLK(CLK), .RST(RST), .DIN(aluC), .DOUT(adr));
  assign REGNUM = ENABLE ? SRC1 : 5'bz;  // Controlled_Buffer controlled_buffer_3
  assign immext = {{20{imm[11]}}, imm};  // Bit_Extender bit_extender_1
  assign resLB = {{24{\byte [7]}}, \byte };  // Bit_Extender bit_extender_2
  assign resLBU = {{24{1'b0}}, \byte };  // Bit_Extender bit_extender_3
  assign resLH = {{16{halfword[15]}}, halfword};  // Bit_Extender bit_extender_4
  assign resLHU = {{16{1'b0}}, halfword};  // Bit_Extender bit_extender_5
  D_Flip_Flop d_ff_1 (.D(ENABLE), .clk(CLK), .Q(DONE), .reset(RST));  // open: Qn, preset
  // NoConnect on undriven
  // NoConnect on undriven_2
  assign aluA = ENABLE ? outREG : 32'bz;  // Controlled_Buffer controlled_buffer_4
  Multiplexer #(.select(2), .width(8)) multiplexer_2 (
    .in0(DIN[7:0]), .in1(DIN[15:8]), .in2(DIN[23:16]), .in3(DIN[31:24]), .out(\byte ), .sel(adr[1:0]));
  assign aluB = ENABLE ? immext : 32'bz;  // Controlled_Buffer controlled_buffer_5
  assign aluOp = ENABLE ? 4'b0000 : 4'bz;  // Controlled_Buffer controlled_buffer_6
  or or_1 (RD, ENABLE, DONE);
  assign A = ENABLE ? {2'b00, aluC[31:2]} : 32'bz;  // Controlled_Buffer controlled_buffer_7
  Multiplexer #(.select(3), .width(32)) multiplexer_3 (
    .in0(resLB), .in1(resLH), .in2(DIN), .in4(resLBU), .in5(resLHU), .out(result), .sel(func[2:0]));  // open: in3, in6, in7
  assign inREG = DONE ? result : 32'bz;  // Controlled_Buffer controlled_buffer_8
  assign REGNUM = DONE ? dest : 5'bz;  // Controlled_Buffer controlled_buffer_9

  // Other names for the same wires on the sheet: addr[29:0] = aluC[31:2]; inAdr[31:0] = aluC;
  //   byte_select[1:0] = adr[1:0]; halfword_select = adr[0]; ldAdr = ENABLE; ldREG = DONE; resLW[31:0] = DIN
endmodule
